// Logisim project 10387129_ass4B_prob1.circ as structural Verilog: 1 circuit, main circuit main
module main (
  input  Reset,
  input  in_2,
  input  Clock_input
);

  wire [7:0] adder_1_out, and_1_out, bit_extender_1_out, register_1_q;

  assign bit_extender_1_out = {{7{Reset}}, Reset};  // Bit_Extender bit_extender_1
  assign and_1_out = adder_1_out & ~bit_extender_1_out;  // AND_Gate and_1, 8 bits wide
  Register register_1 (.D(and_1_out), .en(in_2), .Q(register_1_q), .clk(Clock_input));  // open: clr
  Adder adder_1 (.a(register_1_q), .b(8'h1), .out(adder_1_out));  // open: cin, cout
  DotMatrix #(.inputtype("row"), .matrixcols(8), .matrixrows(1)) dotmatrix_1 (.row0(register_1_q));

  // Notes on the sheet:
  //   Bit extender
  //   LED output
endmodule
