// Logisim project 10387129_ass4B_prob2.circ as structural Verilog: 1 circuit, main circuit main
module main (
  input  [7:0] Address_Value,
  input  [7:0] Data_Value,
  input  in_3
);

  wire clock_1_out, not_1_out;
  wire [7:0] ram_1_data;

  Clock clock_1 (.out(clock_1_out));
  RAM #(.bus("separate")) ram_1 (
    .addr(Address_Value), .din(Data_Value), .data(ram_1_data), .str(in_3), .clk(clock_1_out), .ld(not_1_out));  // open: sel, clr
  not not_1 (not_1_out, in_3);
  DotMatrix #(.inputtype("row"), .matrixcols(8), .matrixrows(1)) dotmatrix_1 (.row0(ram_1_data));

  // Notes on the sheet:
  //   Clock input
  //   Load/Store control switch
  //   LED output
endmodule
