// Logisim project 10387129_ass4B_prob3.circ as structural Verilog: 1 circuit, main circuit main
module main (
  input  Reset,
  input  in_2,
  input  [7:0] Manual_Address,
  input  [7:0] Data_Value,
  input  in_5
);

  wire clock_1_out, clock_2_out, not_1_out;
  wire [7:0] adder_1_out, and_1_out, bit_extender_1_out, multiplexer_1_out, ram_1_data, register_1_q;

  assign bit_extender_1_out = {{7{Reset}}, Reset};  // Bit_Extender bit_extender_1
  assign and_1_out = adder_1_out & ~bit_extender_1_out;  // AND_Gate and_1, 8 bits wide
  Multiplexer #(.width(8), .enable("false")) multiplexer_1 (
    .in0(register_1_q), .in1(Manual_Address), .out(multiplexer_1_out), .sel(in_5));
  Register register_1 (.D(and_1_out), .en(in_2), .Q(register_1_q), .clk(clock_1_out));  // open: clr
  Clock clock_1 (.out(clock_1_out));
  Clock clock_2 (.out(clock_2_out));
  not not_1 (not_1_out, in_5);
  Adder adder_1 (.a(register_1_q), .b(8'h1), .out(adder_1_out));  // open: cin, cout
  RAM #(.bus("separate")) ram_1 (
    .addr(multiplexer_1_out), .din(Data_Value), .data(ram_1_data), .str(in_5), .clk(clock_2_out),
    .ld(not_1_out));  // open: sel, clr
  DotMatrix #(.inputtype("row"), .matrixcols(8), .matrixrows(1)) dotmatrix_1 (.row0(ram_1_data));

  // Notes on the sheet:
  //   Bit extender
  //   Multiplexer
  //   Store/Load control switch
  //   RAM block
  //   8-bit adder
  //   LED output
endmodule
