// Logisim project team18_ass5.circ as structural Verilog: 10 circuits, main circuit main
module main (
  input  [7:0] RAM_Input_Data,
  input  Reset_bar,
  input  RAM_Write_Enable,
  output [1:0] opcode,
  output [1:0] rs,
  output [1:0] rt,
  output [1:0] rd_offset_const
);

  wire Clk_out, control_circuit_1_alusrc, control_circuit_1_memtoreg, control_circuit_1_memwrite,
       control_circuit_1_regwrite, control_circuit_1_writereg;
  wire [1:0] multiplexer_2_out;
  wire [3:0] alu_1_alu_output, bit_extender_1_out, data_ram_1_dataout, multiplexer_1_out, multiplexer_3_out,
       register_file_1_readdata1, register_file_1_readdata2;
  wire [7:0] program_counter_1_output;

  Clock Clk (.out(Clk_out));
  Program_Counter program_counter_1 (.Reset(Reset_bar), .Clock_input(Clk_out), .Output(program_counter_1_output));
  Program_RAM_2 program_ram_2_1 (
    .Address_Value(program_counter_1_output), .Data_Value(RAM_Input_Data), .in_3(Reset_bar),
    .DataOut({opcode, rs, rt, rd_offset_const}));
  assign bit_extender_1_out = {{2{1'b0}}, rd_offset_const};  // Bit_Extender bit_extender_1
  Control_Circuit control_circuit_1 (
    .opcode(opcode), .ALUSRc(control_circuit_1_alusrc), .WriteReg(control_circuit_1_writereg),
    .RegWrite(control_circuit_1_regwrite), .MemWrite(control_circuit_1_memwrite),
    .MemtoReg(control_circuit_1_memtoreg));
  Multiplexer #(.width(4), .enable("false")) multiplexer_1 (
    .in0(data_ram_1_dataout), .in1(alu_1_alu_output), .out(multiplexer_1_out),
    .sel(control_circuit_1_memtoreg));
  Multiplexer #(.width(2), .enable("false")) multiplexer_2 (
    .in0(rt), .in1(rd_offset_const), .out(multiplexer_2_out), .sel(control_circuit_1_writereg));
  Register_File register_file_1 (
    .WriteData(multiplexer_1_out), .WriteReg(multiplexer_2_out), .RegWrite(control_circuit_1_regwrite),
    .Clock(Clk_out), .ReadData1(register_file_1_readdata1), .ReadReg1(rs),
    .ReadData2(register_file_1_readdata2), .ReadReg2(rt));
  Multiplexer #(.width(4), .enable("false")) multiplexer_3 (
    .in0(bit_extender_1_out), .in1(register_file_1_readdata2), .out(multiplexer_3_out),
    .sel(control_circuit_1_alusrc));
  ALU alu_1 (
    .Input1(register_file_1_readdata1), .Input2(multiplexer_3_out), .opcode(opcode),
    .ALU_Output(alu_1_alu_output));
  Data_RAM data_ram_1 (
    .Address(alu_1_alu_output), .DataIn(register_file_1_readdata2), .DataOut(data_ram_1_dataout),
    .Write(control_circuit_1_memwrite), .Clk(Clk_out), .Reset(Reset_bar));
endmodule

module Full_Adder (
  input  Carry_In,
  input  X,
  input  Y,
  output Sum,
  output Carry_Out
);

  wire and_1_out, and_2_out, xor_1_out;

  and and_1 (and_1_out, X, Y);
  xor xor_1 (xor_1_out, X, Y);
  and and_2 (and_2_out, Carry_In, xor_1_out);
  xor xor_2 (Sum, Carry_In, xor_1_out);
  or or_1 (Carry_Out, and_2_out, and_1_out);
endmodule

module _4_Bit_Adder (
  input  Y3,
  input  X3,
  input  Y2,
  input  X2,
  input  Y1,
  input  X1,
  input  Y0,
  input  X0,
  output Sum,
  output Sum_2,
  output Sum_3,
  output Output1
);

  wire full_adder_1_p5, full_adder_2_p5, full_adder_3_p5;

  // Full_Adder full_adder_1: pin names not known; wires that end beside it: Y3, 1'b0, X3, Sum, full_adder_1_p5
  // Full_Adder full_adder_2: pin names not known; wires that end beside it: Y2, full_adder_1_p5, X2, Sum_2, full_adder_2_p5
  // Full_Adder full_adder_3: pin names not known; wires that end beside it: Y1, full_adder_2_p5, X1, Sum_3, full_adder_3_p5
  // Full_Adder full_adder_4: pin names not known; wires that end beside it: Y0, full_adder_3_p5, X0, Output1, 1'b0
endmodule

module ALU (
  input  [3:0] Input1,
  input  [3:0] Input2,
  input  [1:0] opcode,
  output [3:0] ALU_Output
);

  wire [3:0] multiplexer_1_out;

  Multiplexer #(.select(2), .width(4), .enable("false")) multiplexer_1 (
    .in0(Input2), .in1(Input2), .in2(Input2), .in3(Input2), .out(multiplexer_1_out), .sel(opcode));
  _4_Bit_Adder u_4_bit_adder_1 (
    .Y3(multiplexer_1_out[3]), .X3(Input1[3]), .Y2(multiplexer_1_out[2]), .X2(Input1[2]),
    .Y1(multiplexer_1_out[1]), .X1(Input1[1]), .Y0(multiplexer_1_out[0]), .X0(Input1[0]),
    .Sum(ALU_Output[3]), .Sum_2(ALU_Output[2]), .Sum_3(ALU_Output[1]), .Output1(ALU_Output[0]));
endmodule

module Instruction_Memory (
  input  [7:0] RAM_Input_Data,
  input  Reset_bar,
  input  RAM_Write_Enable,
  output [7:0] PC_Output
);

  wire clock_1_out, program_counter_1_p3;

  Clock clock_1 (.out(clock_1_out));
  // Program_Counter program_counter_1: pin names not known; wires that end beside it: Reset_bar, clock_1_out, program_counter_1_p3
  // Program_RAM_2 program_ram_2_1: pin names not known; wires that end beside it: RAM_Input_Data, program_counter_1_p3, RAM_Write_Enable, clock_1_out, PC_Output
endmodule

// Reg File
module Register_File (
  input  [3:0] WriteData,
  input  [1:0] WriteReg,
  input  [1:0] ReadReg1,
  input  [1:0] ReadReg2,
  input  RegWrite,
  input  Clock,
  output [3:0] ReadData1,
  output [3:0] ReadData2
);

  wire and_1_out, and_2_out, and_3_out, and_4_out, decoder_1_out0, decoder_1_out1, decoder_1_out2,
       decoder_1_out3;
  wire [3:0] multiplexer_1_out, multiplexer_2_out, multiplexer_3_out, multiplexer_4_out, register_1_q,
       register_2_q, register_3_q, register_4_q;

  Decoder #(.select(2), .enable("false")) decoder_1 (
    .out0(decoder_1_out0), .out1(decoder_1_out1), .out2(decoder_1_out2), .out3(decoder_1_out3), .sel(WriteReg));
  and and_1 (and_1_out, decoder_1_out0, RegWrite);
  and and_2 (and_2_out, decoder_1_out1, RegWrite);
  and and_3 (and_3_out, decoder_1_out2, RegWrite);
  and and_4 (and_4_out, decoder_1_out3, RegWrite);
  Multiplexer #(.width(4), .enable("false")) multiplexer_1 (
    .in0(register_1_q), .in1(WriteData), .out(multiplexer_1_out), .sel(and_1_out));
  Multiplexer #(.width(4), .enable("false")) multiplexer_2 (
    .in0(register_2_q), .in1(WriteData), .out(multiplexer_2_out), .sel(and_2_out));
  Multiplexer #(.width(4), .enable("false")) multiplexer_3 (
    .in0(register_3_q), .in1(WriteData), .out(multiplexer_3_out), .sel(and_3_out));
  Multiplexer #(.width(4), .enable("false")) multiplexer_4 (
    .in0(register_4_q), .in1(WriteData), .out(multiplexer_4_out), .sel(and_4_out));
  Register #(.width(4)) register_1 (.D(multiplexer_1_out), .Q(register_1_q), .clk(Clock));  // open: en, clr
  Register #(.width(4)) register_2 (.D(multiplexer_2_out), .Q(register_2_q), .clk(Clock));  // open: en, clr
  Register #(.width(4)) register_3 (.D(multiplexer_3_out), .Q(register_3_q), .clk(Clock));  // open: en, clr
  Register #(.width(4)) register_4 (.D(multiplexer_4_out), .Q(register_4_q), .clk(Clock));  // open: en, clr
  Multiplexer #(.select(2), .width(4), .enable("false")) multiplexer_5 (
    .in0(register_1_q), .in1(register_2_q), .in2(register_3_q), .in3(register_4_q), .out(ReadData1),
    .sel(ReadReg1));
  Multiplexer #(.select(2), .width(4), .enable("false")) multiplexer_6 (
    .in0(register_1_q), .in1(register_2_q), .in2(register_3_q), .in3(register_4_q), .out(ReadData2),
    .sel(ReadReg2));

  // Notes on the sheet:
  //   Register File 4x4-bits
endmodule

// D RAM
module Data_RAM (
  input  [3:0] Address,
  input  [3:0] DataIn,
  input  Write,
  input  Reset,
  input  Clk,
  output [3:0] DataOut
);

  RAM #(.addrWidth(4), .dataWidth(4), .bus("separate")) ram_1 (
    .addr(Address), .din(DataIn), .data(DataOut), .str(Write), .clk(Clk), .clr(Reset));  // open: sel, ld
endmodule

// PC
module Program_Counter (
  input  Reset,
  input  Clock_input,
  output [7:0] Output
);

  wire [7:0] adder_1_out, and_1_out, bit_extender_1_out;

  assign bit_extender_1_out = {{7{Reset}}, Reset};  // Bit_Extender bit_extender_1
  Register register_1 (.D(and_1_out), .Q(Output), .clk(Clock_input));  // open: en, clr
  assign and_1_out = adder_1_out & ~bit_extender_1_out;  // AND_Gate and_1, 8 bits wide
  Adder adder_1 (.a(Output), .b(8'h1), .out(adder_1_out));  // open: cin, cout
  DotMatrix #(.inputtype("row"), .matrixcols(1), .matrixrows(8)) dotmatrix_1 (
    .row0(Output[0]), .row1(Output[1]), .row2(Output[2]), .row3(Output[3]), .row4(Output[4]),
    .row5(Output[5]), .row6(Output[6]), .row7(Output[7]));

  // Notes on the sheet:
  //   Bit extender
endmodule

// PRAM
module Program_RAM_2 (
  input  [7:0] Address_Value,
  input  [7:0] Data_Value,
  input  in_3,
  output [7:0] DataOut
);

  wire clock_1_out, not_1_out, undriven;

  Clock clock_1 (.out(clock_1_out));
  not not_1 (not_1_out, in_3);
  RAM #(.bus("separate")) ram_1 (
    .addr(Address_Value), .din(Data_Value), .data(DataOut), .str(in_3), .clk(clock_1_out), .ld(not_1_out),
    .clr(undriven));  // open: sel
  DotMatrix #(.matrixcols(8), .matrixrows(1)) dotmatrix_1 (
    .col0(DataOut[7]), .col1(DataOut[6]), .col2(DataOut[5]), .col3(DataOut[4]), .col4(DataOut[3]),
    .col5(DataOut[2]), .col6(DataOut[1]), .col7(DataOut[0]));

  // Notes on the sheet:
  //   Clock input
  //   Load/Store control switch
endmodule

// Cntrl
module Control_Circuit (
  input  [1:0] opcode,
  output ALUSRc,
  output WriteReg,
  output RegWrite,
  output MemWrite,
  output MemtoReg
);

  wire not_1_out;

  and and_1 (ALUSRc, opcode[1], opcode[0]);
  not not_1 (not_1_out, opcode[1]);
  nand nand_1 (RegWrite, not_1_out, opcode[0]);
  not not_2 (MemWrite, RegWrite);

  assign MemtoReg = opcode[1];
  assign WriteReg = ALUSRc;
endmodule
